# Fritzing sketch NodeMCU lolin Temperature relay lcd (saved by Fritzing 0.9.3b)
breadboards: 1

parts:
  U1 = NodeMCU V3.0
  Part1 = LCD1602-I2C
  DS1 = DS18B20 1-Wire Temperature Sensor [part_number=DS18B20]
  U2 = 2-Channel 5v Relay Shield [package=relay-2ch5v10a]
  R1 = Resistor [tolerance=±5% resistance=4.7k package=THT]
  LED4 = LEDs [package=led10mm]
  LED5 = LEDs [package=led10mm]
  Part3 = Lilypad Battery Connect
  S1 = Momentary Switch [package=ksa_sealed_tac_switch]
  S2 = Momentary Switch [package=ksa_sealed_tac_switch]
  R2 = Resistor [tolerance=±5% resistance=470 package=THT]
  R3 = Resistor [tolerance=±5% resistance=470 package=THT]

nets (from the breadboard view):
  N1: U1.D1, Part1.SCL
  N2: U1.D2, Part1.SDA
  N3: U1.D3, S2.2, R2.Pin_0
  N4: U1.3V3, R2.Pin_1, R3.Pin_1
  GND: U1.GND, Part1.GND, DS1.GND, U2.GND, S1.1, S2.1
  N5: U1.D5, DS1.DQ, R1.Pin_0
  N6: U1.D6, U2.IN2
  N7: U1.D7, U2.IN1
  N8: U1.D8, S1.2, R3.Pin_0
  VCC: U1.Vin, Part1.VCC, DS1.VDD, U2.VCC, R1.Pin_1
  N9: U2.K1-In, LED5.A
  N10: U2.K1-On, U2.K2-On, Part3.+
  N11: U2.K2-In, LED4.A
  N12: LED4.C, LED5.C, Part3.-

notes:
  240V AC power supply

custom parts:
  NodeMCU V3.0: ESP8266 based NodeMCU
  LCD1602-I2C: A standard character display, usually with 2x16 characters. Comes in many colors with LCM1602 IIC attached.
  2-Channel 5v Relay Shield: 2 Channel 5v Relay Shield w. 2x SPD-06VDC-SD-C
  LEDs: LEDs Standard schematic elements and footprints for 5mm, 3mm, 1206, and 0603 sized LEDs. 5mm - Spark Fun Electronics SKU : COM-00529 (and others)

// code stored in the sketch: NodemcuTemperatureRelayLcd.ino
/********************** LYBRARY ****************************/

#define BLYNK_PRINT Serial // Comment this out to disable prints and save space


#include <ESP8266WiFi.h>
#include <BlynkSimpleEsp8266.h>
#include <OneWire.h>
#include <DallasTemperature.h>
#include <LiquidCrystal_I2C.h>

/* TIMER */
#include <SimpleTimer.h>
SimpleTimer timer;

/********************** BLYNK ACCOUNT ****************************/
char auth[] = "BLYNK_TOKEN";
char ssid[] = "SSID";
char pass[] = "PASS";


/********************** HARDWARE ****************************/
// Temperature sensor full ID, including family code and CRC
// use OneWire Scanner to get the address
DeviceAddress tempSensor = { 0x28, 0xFF, 0x64, 0x1D, 0x8F, 0x87, 0x95, 0xB1 };

// Pin used for the OneWire interface
#define ONE_WIRE_BUS 14 //pin D5 nodemcu Lolin v3

LiquidCrystal_I2C lcd(0x27, 16, 2); //LCD address and type.
//D2 = SDA D1 = SCL

/**************BIG CHAR*********************************************/


/********************** TEMPERATURE DEF****************************/
OneWire oneWire(ONE_WIRE_BUS);
DallasTemperature DS18B20(&oneWire);
float temp;

/********************** SETUP ****************************/
void setup()
{
  // Debug console
  Serial.begin(9600);
  Blynk.begin(auth, ssid, pass, IPAddress(188,166,206,43), 8080); //use other method to connect to blynk server
  DS18B20.begin();
  timer.setInterval(15000L, getSendData);
  Blynk.syncAll();

  pinMode(2, OUTPUT);
  
  lcd.init();
  lcd.backlight();
  lcd.clear();

}

/********************** LOOP ****************************/
void loop()
{
  Blynk.run();
  timer.run();
}

/********************** Send Sensor data to Blynk ****************************/
void getSendData()
{
  DS18B20.requestTemperatures(); 
  temp = DS18B20.getTempCByIndex(0);
  Serial.println(temp);
  Blynk.virtualWrite(10, temp); //virtual pin V10
  
  lcd.setCursor(0, 0);
  lcd.print("Temp:");
  lcd.setCursor(6,0);
  lcd.print(temp);
  lcd.setCursor(12,0);
  lcd.print("'C");
}
