# Fritzing sketch c02_digitalread (saved by Fritzing 0.9.3b)
breadboards: 1

parts:
  Part1 = Arduino Uno (Rev3)
  LED1 = LED - 5mm [color="Red (633nm)" package="5 mm [THT]"]
  R1 = Resistor [tolerance=±5% resistance=320 package=THT]
  S1 = Pushbutton [package=THT]
  R2 = Resistor [tolerance=±5% resistance=220 package=THT]

nets:
  N1: Part1.D2, S1.leg0, R2.Pin_0
  N2: Part1.D3_PWM, R1.Pin_1
  N3: Part1.5V, S1.leg1
  N4: Part1.GND, LED1.cathode, R2.Pin_1
  N5: LED1.anode, R1.Pin_0
