# Fritzing sketch c06_analogread (saved by Fritzing 0.9.3b)
breadboards: 1

parts:
  Part1 = Arduino Uno (Rev3)
  LED1 = LED - 5mm [color="Red (633nm)" package="5 mm [THT]"]
  R1 = Resistor [tolerance=±5% resistance=320 package=THT]
  R3 = Rotary Potentiometer (Small) [maximum_resistance=100kΩ package=THT]

nets:
  N1: Part1.A0, R3.wiper
  N2: Part1.D3_PWM, R1.Pin_1
  N3: Part1.5V, R3.leg2
  N4: Part1.GND, LED1.cathode, R3.leg1
  N5: LED1.anode, R1.Pin_0
