# Fritzing sketch c07_pulsein (saved by Fritzing 0.9.3b)
breadboards: 1

parts:
  Part1 = Arduino Uno (Rev3)
  LED1 = LED - 5mm [color="Red (633nm)" package="5 mm [THT]"]
  R1 = Resistor [tolerance=±5% resistance=320 package=THT]
  Part2 = SRF05 Ultrasonic Rangefinder

nets:
  N1: Part1.D9_PWM, Part2.Echo
  N2: Part1.D10_PWM/SS, Part2.Trig
  N3: Part1.D3_PWM, R1.Pin_1
  5V: Part1.5V, Part2.VCC
  GND: Part1.GND, LED1.cathode, Part2.GND
  N4: LED1.anode, R1.Pin_0
