# Fritzing sketch c09_servo (saved by Fritzing 0.9.3b)
breadboards: 1

parts:
  Part1 = Arduino Uno (Rev3)
  R3 = Rotary Potentiometer (Small) [maximum_resistance=100kΩ package=THT]
  J1 = Basic Servo

nets:
  N1: Part1.A0, R3.wiper
  N2: Part1.D3_PWM, J1.pulse
  5V: Part1.5V, R3.leg2, J1.vcc
  GND: Part1.GND, R3.leg1, J1.gnd
