# Fritzing sketch c10_dht (saved by Fritzing 0.9.3b)
breadboards: 1

parts:
  Part1 = Arduino Uno (Rev3)
  DHT1 = DHT22 Humidity and Temperature Sensor
  R1 = Resistor [tolerance=±5% resistance=4.7k package=THT]

nets:
  N1: Part1.D3_PWM, DHT1.DATA, R1.Pin_0
  5V: Part1.5V, DHT1.VDD, R1.Pin_1
  GND: Part1.GND, DHT1.GND
