# Fritzing sketch c11_relay (saved by Fritzing 0.9.3b)
breadboards: 1

parts:
  Part1 = Arduino Uno (Rev3)
  U1 = 2-Channel 5v Relay Shield [package=relay-2ch5v10a]

nets:
  N1: Part1.D3_PWM, U1.IN1
  5V: Part1.5V, U1.VCC
  GND: Part1.GND, U1.GND

custom parts:
  2-Channel 5v Relay Shield: 2 Channel 5v Relay Shield w. 2x SPD-06VDC-SD-C
