# Fritzing sketch c13_lcd (saved by Fritzing 0.9.3b)
breadboards: 1

parts:
  Matrix_keypad1 = KEYPAD 4x4
  LCD1 = LCD screen
  R1 = Resistor [tolerance=±5% resistance=220 package=THT]
  R2 = Trimmer Potentiometer [maximum_resistance=10kΩ package=THT]
  Part2 = Arduino Mega ADK (Rev3)

nets:
  N1: Matrix_keypad1.col1, Part2.D35
  N2: Matrix_keypad1.col2, Part2.D37
  N3: Matrix_keypad1.col3, Part2.D39
  N4: Matrix_keypad1.col4, Part2.D41
  N5: Matrix_keypad1.row1, Part2.D43
  N6: Matrix_keypad1.row2, Part2.D45
  N7: Matrix_keypad1.row3, Part2.D47
  N8: Matrix_keypad1.row4, Part2.D49
  VSS: LCD1.VSS, LCD1.R/W, LCD1.LED-, R2.leg1, Part2.GND
  VDD: LCD1.VDD, R1.Pin_1, R2.leg2, Part2.5V
  N9: LCD1.V0, R2.wiper
  N10: LCD1.RS, Part2.D33
  N11: LCD1.E, Part2.D31
  N12: LCD1.DB4, Part2.D29
  N13: LCD1.DB5, Part2.D27
  N14: LCD1.DB6, Part2.D25
  N15: LCD1.DB7, Part2.D23
  N16: LCD1.LED+, R1.Pin_0

notes:
  R1
  R2
  R3
  R4
  C1
  C2
  C3
  C4

custom parts:
  KEYPAD 4x4: Matrix keypad 16 buttons, 4 rows x 4 columns
